# Fritzing sketch Emetteur (saved by Fritzing 0.9.0b)
breadboards: 1

parts:
  Composant1 = Arduino Pro Mini v13
  RHT1 = Humidity and Temperature Sensor RHT03
  R1 = Resistor [package="2010 [SMD]"]
  LED1 = smd LED [color="Red (633nm)" package="1206 [SMD]"]

nets:
  VCC: Composant1.VCC, RHT1.Vcc, R1.Pin_0
  N1: Composant1.GND, RHT1.GND_2, LED1.cathode
  N2: Composant1.D8, RHT1.Data-signal, R1.Pin_1

notes:
  Station Météo Arduino - Eih3Prog
  10k
  DHT11
